// Logisim project watermelon_one.circ as structural Verilog: 6 circuits, main circuit main
module main (
);

  program_counter program_counter_1 ();  // open: Y, OE, WE, C, CL, D, SW, O
  // ROM #(.addrWidth(19), .line("quad")) rom_1: pin names not known
endmodule

module octal_D_flip_flop (
  input  OE,
  input  C,
  input  CL,
  input  [7:0] D,
  output [7:0] O
);

  wire [7:0] d_ff_1_q;

  D_Flip_Flop d_ff_1 (.D(D[0]), .clk(C), .Q(d_ff_1_q[0]), .reset(CL));  // open: Qn, preset
  D_Flip_Flop d_ff_2 (.D(D[1]), .clk(C), .Q(d_ff_1_q[1]), .reset(CL));  // open: Qn, preset
  D_Flip_Flop d_ff_3 (.D(D[2]), .clk(C), .Q(d_ff_1_q[2]), .reset(CL));  // open: Qn, preset
  D_Flip_Flop d_ff_4 (.D(D[3]), .clk(C), .Q(d_ff_1_q[3]), .reset(CL));  // open: Qn, preset
  D_Flip_Flop d_ff_5 (.D(D[4]), .clk(C), .Q(d_ff_1_q[4]), .reset(CL));  // open: Qn, preset
  D_Flip_Flop d_ff_6 (.D(D[5]), .clk(C), .Q(d_ff_1_q[5]), .reset(CL));  // open: Qn, preset
  D_Flip_Flop d_ff_7 (.D(D[6]), .clk(C), .Q(d_ff_1_q[6]), .reset(CL));  // open: Qn, preset
  D_Flip_Flop d_ff_8 (.D(D[7]), .clk(C), .Q(d_ff_1_q[7]), .reset(CL));  // open: Qn, preset
  assign O = OE ? d_ff_1_q : 8'bz;  // Controlled_Buffer controlled_buffer_1
endmodule

module register_8_bit (
  input  OE,
  input  WE,
  input  C,
  input  CL,
  input  [7:0] D,
  output [7:0] O
);

  wire and_1_out;

  and and_1 (and_1_out, WE, C);
  octal_D_flip_flop octal_d_flip_flop_1 (.OE(OE), .C(and_1_out), .CL(CL), .D(D), .O(O));
endmodule

module sram (
  input  in_1,
  input  in_2,
  input  in_3,
  input  in_4
);

  RAM #(.readbehav("war")) ram_1 ();  // open: addr, we, oe, clk, din, dout
  RAM #(.readbehav("war")) ram_2 ();  // open: addr, we, oe, clk, din, dout
  RAM #(.readbehav("war")) ram_3 ();  // open: addr, we, oe, clk, din, dout
  RAM #(.readbehav("war")) ram_4 ();  // open: addr, we, oe, clk, din, dout
endmodule

module program_counter (
  input  [7:0] Y,
  input  OE,
  input  WE,
  input  C,
  input  CL,
  input  [7:0] D,
  input  SW,
  output [7:0] O
);

  wire not_1_out;
  wire [7:0] adder_1_out, controlled_buffer_1_out;

  assign controlled_buffer_1_out = not_1_out ? adder_1_out : 8'bz;  // Controlled_Buffer controlled_buffer_1
  not not_1 (not_1_out, SW);
  assign controlled_buffer_1_out = SW ? D : 8'bz;  // Controlled_Buffer controlled_buffer_2
  Adder adder_1 (.a(Y), .b(O), .out(adder_1_out));  // open: cin, cout
  register_8_bit register_8_bit_1 (.OE(OE), .WE(WE), .C(C), .CL(CL), .D(controlled_buffer_1_out), .O(O));

  // Notes on the sheet:
  //   Y: initial=0x4
endmodule

module register_file (
  input  [4:0] RA,
  input  WE,
  input  OE,
  input  C,
  input  [31:0] D,
  output [31:0] O
);

  RAM #(.addrWidth(5), .readbehav("war")) ram_1 (.addr(RA), .we(WE), .oe(OE), .clk(C), .din(D[7:0]), .dout(O[7:0]));
  RAM #(.addrWidth(5), .readbehav("war")) ram_2 (.addr(RA), .we(WE), .oe(OE), .clk(C), .din(D[23:16]), .dout(O[23:16]));
  RAM #(.addrWidth(5), .readbehav("war")) ram_3 (.addr(RA), .we(WE), .oe(OE), .clk(C), .din(D[15:8]), .dout(O[15:8]));
  RAM #(.addrWidth(5), .readbehav("war")) ram_4 (.addr(RA), .we(WE), .oe(OE), .clk(C), .din(D[31:24]), .dout(O[31:24]));
endmodule
